// Logisim project led_aula_isis.circ as structural Verilog: 1 circuit, main circuit main
module main (
  input  a,
  input  b,
  input  c,
  input  d
);

  wire and_1_out, and_2_out, and_3_out, and_4_out, and_5_out, and_6_out, and_7_out, and_8_out, and_9_out,
       and_10_out, and_11_out, nor_1_out, nor_2_out, nor_3_out, nor_4_out, nor_5_out, not_1_out, not_2_out,
       not_3_out, not_4_out, not_5_out, not_6_out, not_7_out, not_8_out, not_9_out, not_10_out, not_11_out,
       or_1_out, or_2_out, or_3_out, or_4_out, or_5_out, or_6_out, or_7_out;

  not not_1 (not_1_out, c);
  and and_1 (and_1_out, b, d);
  nor nor_1 (nor_1_out, b, d);
  not not_2 (not_2_out, b);
  and and_2 (and_2_out, c, d);
  nor nor_2 (nor_2_out, c, d);
  not not_3 (not_3_out, c);
  not not_4 (not_4_out, b);
  nor nor_3 (nor_3_out, b, d);
  not not_5 (not_5_out, d);
  not not_6 (not_6_out, c);
  not not_7 (not_7_out, d);
  not not_8 (not_8_out, b);
  and and_3 (and_3_out, not_4_out, c);
  not not_9 (not_9_out, d);
  and and_4 (and_4_out, b, not_1_out, d);
  and and_5 (and_5_out, c, not_5_out);
  nor nor_4 (nor_4_out, b, d);
  not not_10 (not_10_out, c);
  not not_11 (not_11_out, d);
  nor nor_5 (nor_5_out, c, d);
  and and_6 (and_6_out, b, not_6_out);
  and and_7 (and_7_out, b, not_7_out);
  and and_8 (and_8_out, not_8_out, c);
  or or_1 (or_1_out, a, c, and_1_out, nor_1_out);
  or or_2 (or_2_out, not_2_out, and_2_out, nor_2_out);
  or or_3 (or_3_out, not_3_out, b, d);
  and and_9 (and_9_out, c, not_9_out);
  or or_4 (or_4_out, and_5_out, nor_4_out);
  and and_10 (and_10_out, not_10_out, b);
  and and_11 (and_11_out, b, not_11_out);
  or or_5 (or_5_out, a, and_6_out, and_7_out, and_8_out);
  or or_6 (or_6_out, a, and_3_out, and_9_out, nor_3_out, and_4_out);
  or or_7 (or_7_out, a, and_10_out, and_11_out, nor_5_out);
  _7_Segment_Display u_7_segment_display_1 (
    .g(or_5_out), .f(or_7_out), .a(or_1_out), .b(or_2_out), .e(or_4_out), .d(or_6_out), .c(or_3_out));  // open: dp

  // Notes on the sheet:
  //   A
  //   B
  //   C
  //   E
  //   G
  //   D
  //   F
endmodule
